// Logisim project test.circ as structural Verilog: 1 circuit, main circuit main
module main (
);

  // NAND_Gate nand_1 is placed but not wired
  // NAND_Gate nand_2 is placed but not wired
  // NAND_Gate nand_3 is placed but not wired
  // NAND_Gate nand_4 is placed but not wired
  // NAND_Gate nand_5 is placed but not wired
  // NAND_Gate nand_6 is placed but not wired
  // NAND_Gate nand_7 is placed but not wired
  // NAND_Gate nand_8 is placed but not wired
endmodule
